# Fritzing sketch HelloWorld (saved by Fritzing 1.0.7)
breadboards: 1

parts:
  U1 = ESP32-38PinWide [part_number=ESP32-38PinWide]
  S2 = Momentary Switch [package=ksa_sealed_tac_switch]
  LED1 = LED - 3mm [color="Red (633nm)" current=0.030A package="3 mm [THT]"]
  R1 = Resistor [tolerance=±5% resistance=220 package="0805 [SMD]"]

nets:
  N1: U1.GND, S2.2, LED1.cathode
  N2: U1.GPIO4, R1.Pin_1
  N3: U1.GPIO5, S2.3
  N4: LED1.anode, R1.Pin_0

custom parts:
  ESP32-38PinWide: Generic 38-Pin ESP32 with wide format (only access to one side of pins on a breadboard) based on Stephen Lilley's HiLetgo ESP-WROOM-32 ESP32 ESP-32S Development Board.
