# Fritzing sketch PhotoCell (saved by Fritzing 1.0.7)
breadboards: 1

parts:
  U1 = ESP32-38PinWide [part_number=ESP32-38PinWide]
  R1 = Photocell (LDR) [power=0.25W dark_resistance_@0.01lx=300kΩ light_resistance_@100lx=400Ω luminance=10lx package=THT]
  R2 = Resistor [tolerance=±5% resistance=10k package="0805 [SMD]"]
  LED1 = smd LED [color="Red (633nm)" package="0805 [SMD]"]
  R3 = Resistor [tolerance=±5% resistance=220 package="0805 [SMD]"]

nets:
  N1: U1.3.3, R1.pin_0
  N2: U1.GND, R2.Pin_1, LED1.cathode
  N3: U1.GPIO2, R3.Pin_0
  N4: U1.GPIO4, R1.pin_1, R2.Pin_0
  N5: LED1.anode, R3.Pin_1

custom parts:
  ESP32-38PinWide: Generic 38-Pin ESP32 with wide format (only access to one side of pins on a breadboard) based on Stephen Lilley's HiLetgo ESP-WROOM-32 ESP32 ESP-32S Development Board.
