# Fritzing sketch TrafficLight (saved by Fritzing 1.0.7)
breadboards: 1

parts:
  U1 = ESP32-38PinWide [part_number=ESP32-38PinWide]
  S1 = Momentary Switch [package=ksa_sealed_tac_switch]
  LED1 = LED - 3mm [color="Red (633nm)" current=0.030A package="3 mm [THT]"]
  LED2 = LED - 3mm [color="Yellow (595nm)" current=0.030A package="3 mm [THT]"]
  LED3 = LED - 3mm [color="Green (570nm)" current=0.030A package="3 mm [THT]"]
  R1 = Resistor [tolerance=±5% resistance=220 package="0805 [SMD]"]
  R2 = Resistor [tolerance=±5% resistance=220 package="0805 [SMD]"]
  R3 = Resistor [tolerance=±5% resistance=220 package="0805 [SMD]"]

nets:
  N1: U1.GND, S1.2, LED1.cathode, LED2.cathode, LED3.cathode
  N2: U1.GPIO15, R1.Pin_1
  N3: U1.GPIO2, R2.Pin_1
  N4: U1.GPIO4, R3.Pin_1
  N5: U1.GPIO5, S1.3
  N6: LED1.anode, R3.Pin_0
  N7: LED2.anode, R2.Pin_0
  N8: LED3.anode, R1.Pin_0

custom parts:
  ESP32-38PinWide: Generic 38-Pin ESP32 with wide format (only access to one side of pins on a breadboard) based on Stephen Lilley's HiLetgo ESP-WROOM-32 ESP32 ESP-32S Development Board.
