# Fritzing sketch LedRGB (saved by Fritzing 1.0.7)
breadboards: 1

parts:
  LED1 = RGB LED - (4 legs) [color="Red (633nm)" current=0.030A package="5 mm [THT]"]
  U1 = ESP32-38PinWide [part_number=ESP32-38PinWide]
  R1 = Resistor [tolerance=±5% power=0.25W resistance=220 package=THT]
  R2 = Resistor [tolerance=±5% power=0.25W resistance=220 package=THT]
  R3 = Resistor [tolerance=±5% power=0.25W resistance=220 package=THT]
  R5 = Rotary Potentiometer (Small) [maximum_resistance=100kΩ knob_status=50% power=0.5W package=THT]
  S1 = Momentary Switch [package=ksa_sealed_tac_switch]
  S2 = Momentary Switch [package=ksa_sealed_tac_switch]
  S3 = Momentary Switch [package=ksa_sealed_tac_switch]

nets:
  N1: LED1.red_cathode, R1.Pin_1
  N2: LED1.common_anode, U1.GND, R5.leg2, S1.2, S2.2, S3.2
  N3: LED1.green_cathode, R2.Pin_1
  N4: LED1.blue_cathode, R3.Pin_1
  N5: U1.3.3, R5.leg1
  N6: U1.GPIO34, R5.wiper
  N7: U1.GPIO32, R2.Pin_0
  N8: U1.GPIO33, R3.Pin_0
  N9: U1.GPIO25, R1.Pin_0
  N10: U1.GPIO15, S1.3
  N11: U1.GPIO2, S2.3
  N12: U1.GPIO4, S3.3

custom parts:
  ESP32-38PinWide: Generic 38-Pin ESP32 with wide format (only access to one side of pins on a breadboard) based on Stephen Lilley's HiLetgo ESP-WROOM-32 ESP32 ESP-32S Development Board.
