# Fritzing sketch ServoBLE (saved by Fritzing 1.0.7)
breadboards: 1

parts:
  U1 = ESP32-38PinWide [part_number=ESP32-38PinWide]
  J1 = Basic Servo
  S1 = Pushbutton [package="[SMD]"]
  S2 = Pushbutton [package="[SMD]"]

nets:
  N1: U1.GPIO25, S1.Pin_3, S1.Pin_4
  N2: U1.GPIO26, S2.Pin_3, S2.Pin_4
  GND: U1.GND, J1.gnd, S1.Pin_1, S1.Pin_2, S2.Pin_1, S2.Pin_2
  VIN: U1.VIN, J1.vcc
  N3: U1.GPIO18, J1.pulse

custom parts:
  ESP32-38PinWide: Generic 38-Pin ESP32 with wide format (only access to one side of pins on a breadboard) based on Stephen Lilley's HiLetgo ESP-WROOM-32 ESP32 ESP-32S Development Board.
