# Fritzing sketch TemperatureBLE (saved by Fritzing 1.0.7)
breadboards: 1

parts:
  U1 = ESP32-38PinWide [part_number=ESP32-38PinWide]
  DS1 = DS18B20 1-Wire Temperature Sensor [part_number=DS18B20]
  S1 = Pushbutton [package="[SMD]"]
  R1 = Resistor [tolerance=±5% power=0.25W resistance=4.7k package=THT]
  OLED_I2C1 = OLED 128x64 I2C Monochrome Display

nets:
  VDD: U1.3.3, DS1.VDD, R1.Pin_1, OLED_I2C1.VDD
  N1: U1.GPIO25, S1.Pin_3, S1.Pin_4
  GND: U1.GND, DS1.GND, S1.Pin_1, S1.Pin_2, OLED_I2C1.GND
  N2: U1.GPIO4, DS1.DQ, R1.Pin_0
  N3: U1.GPIO21, OLED_I2C1.SDA
  N4: U1.GPIO22, OLED_I2C1.SCK

custom parts:
  ESP32-38PinWide: Generic 38-Pin ESP32 with wide format (only access to one side of pins on a breadboard) based on Stephen Lilley's HiLetgo ESP-WROOM-32 ESP32 ESP-32S Development Board.
