# Fritzing sketch FMRadio (saved by Fritzing 1.0.7)
breadboards: 1

parts:
  U1 = ESP32-38PinWide [part_number=ESP32-38PinWide]
  OLED_I2C1 = OLED 128x64 I2C Monochrome Display
  M1 = TEA5767 [package=THT]
  S1 = Pushbutton [package="[SMD]"]
  S2 = Pushbutton [package="[SMD]"]
  S3 = Pushbutton [package="[SMD]"]

nets:
  N1: U1.3.3, OLED_I2C1.VDD
  N2: U1.GPIO25, S1.Pin_3, S1.Pin_4
  N3: U1.GPIO26, S2.Pin_3, S2.Pin_4
  N4: U1.GPIO27, S3.Pin_3, S3.Pin_4
  GND: U1.GND, OLED_I2C1.GND, M1.pin4, S1.Pin_1, S1.Pin_2, S2.Pin_1, S2.Pin_2, S3.Pin_1, S3.Pin_2
  N5: U1.VIN, M1.pin1
  N6: U1.GPIO21, OLED_I2C1.SDA, M1.pin2
  N7: U1.GPIO22, OLED_I2C1.SCK, M1.pin3

custom parts:
  ESP32-38PinWide: Generic 38-Pin ESP32 with wide format (only access to one side of pins on a breadboard) based on Stephen Lilley's HiLetgo ESP-WROOM-32 ESP32 ESP-32S Development Board.
  TEA5767: SMAKN brand new 76-108MHZ 5V TEA5767 FM Stereo Radio Module with Cable Antenna for Arduino EK1705(New version)
