# Fritzing sketch ParkingSensor (saved by Fritzing 1.0.7)
breadboards: 1

parts:
  U1 = ESP32-38PinWide [part_number=ESP32-38PinWide]
  Componente1 = Adafruit VL53L1X [part_number="Adafruit #3967"]
  LED2 = RGB LED (com. cathode, rgb) [color="Red (633nm)" current=0.030A package="5 mm [THT]"]
  R1 = Resistor [tolerance=±5% resistance=220 package="2512 [SMD]"]
  R2 = Resistor [tolerance=±5% resistance=220 package="2512 [SMD]"]
  R3 = Resistor [tolerance=±5% resistance=220 package="2512 [SMD]"]

nets:
  N1: U1.3.3, Componente1.VCC
  N2: U1.GPIO25, R1.Pin_0
  N3: U1.GPIO26, R2.Pin_0
  N4: U1.GPIO27, R3.Pin_0
  GND: U1.GND, Componente1.GND, LED2.common_cathode
  N5: U1.GPIO21, Componente1.SDA
  N6: U1.GPIO22, Componente1.SCL
  N7: LED2.red_anode, R1.Pin_1
  N8: LED2.green_anode, R2.Pin_1
  N9: LED2.blue_anode, R3.Pin_1

custom parts:
  ESP32-38PinWide: Generic 38-Pin ESP32 with wide format (only access to one side of pins on a breadboard) based on Stephen Lilley's HiLetgo ESP-WROOM-32 ESP32 ESP-32S Development Board.
  Adafruit VL53L1X: The Adafruit VL53L1X Time of Flight Distance Sensor (also known as VL53L1CX) is a Time of Flight distance sensor that has a massive 4 meter range and LIDAR-like precision. The sensor contains a very tiny invisible laser source and a matching sensor. The VL53L1X can detect the "time of flight", or how long the light has taken to bounce back to the sensor. Since it uses a very narrow light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
