# Fritzing sketch WebServerRelay (saved by Fritzing 1.0.7)
breadboards: 1

parts:
  U1 = ESP32-38PinWide [part_number=ESP32-38PinWide]
  OLED_I2C1 = OLED 128x64 I2C Monochrome Display
  M1 = 1 chan 5v relay module

nets:
  N1: U1.3.3, OLED_I2C1.VDD
  N2: U1.GPIO26, M1.pin_3
  GND: U1.GND, OLED_I2C1.GND, M1.pin_2
  N3: U1.VIN, M1.pin_1
  N4: U1.GPIO21, OLED_I2C1.SDA
  N5: U1.GPIO22, OLED_I2C1.SCK

custom parts:
  ESP32-38PinWide: Generic 38-Pin ESP32 with wide format (only access to one side of pins on a breadboard) based on Stephen Lilley's HiLetgo ESP-WROOM-32 ESP32 ESP-32S Development Board.
  1 chan 5v relay module: 1 Channel 5V Relay Module Board Shield with Optocoupler Support High and Low Level Trigger for Arduino.
