# Fritzing sketch WeatherClock (saved by Fritzing 1.0.7)
breadboards: 1

parts:
  U1 = ESP32-38PinWide [part_number=ESP32-38PinWide]
  LCD1 = 2.8" SPI TFT Module [part_number=MSP2807]
  Componente1 = Adafruit DS3231 [part_number="Adafruit #3013"]
  S1 = Pushbutton [package="[THT]"]

nets:
  N1: U1.3.3, LCD1.pin1, Componente1.Vin
  N2: U1.GPIO32, Componente1.SDA
  N3: U1.GPIO33, Componente1.SCL
  N4: U1.GPIO27, S1.Pin_3, S1.Pin_4
  GND: U1.GND, LCD1.pin2, Componente1.GND, S1.Pin_1, S1.Pin_2
  N5: U1.GPIO15, LCD1.pin8
  N6: U1.GPIO2, LCD1.pin5
  N7: U1.GPIO4, LCD1.pin4
  N8: U1.GPIO5, LCD1.pin3
  N9: U1.GPIO18, LCD1.pin7, LCD1.pin10
  N10: U1.GPIO19, LCD1.pin9, LCD1.pin13
  N11: U1.GPIO21, LCD1.pin11
  N12: U1.GPIO22, LCD1.pin14
  N13: U1.GPIO23, LCD1.pin6, LCD1.pin12

custom parts:
  ESP32-38PinWide: Generic 38-Pin ESP32 with wide format (only access to one side of pins on a breadboard) based on Stephen Lilley's HiLetgo ESP-WROOM-32 ESP32 ESP-32S Development Board.
  2.8" SPI TFT Module: A generic 2.8 inch LCD TFT 320x240 display with touchscreen and SD card slot. Uses the ILI9341 controller, like the Adafruit displays of this size uses.
