# Fritzing sketch AirQuality (saved by Fritzing 1.0.7)
breadboards: 1

parts:
  U1 = ESP32-38PinWide [part_number=ESP32-38PinWide]
  S1 = Pushbutton [package="[SMD]"]
  LED1 = smd LED [color="Red (633nm)" package="0603 [SMD]"]
  R1 = Resistor [tolerance=±5% resistance=220 package="0603 [SMD]"]
  Mod1 = SDS011 - dust sensor [part_number=1]

nets:
  N1: U1.GPIO26, LED1.anode
  N2: U1.GPIO27, S1.Pin_3, S1.Pin_4
  GND: U1.GND, S1.Pin_1, S1.Pin_2, R1.Pin_0, Mod1.GND
  VIN: U1.VIN, Mod1.5V
  N3: U1.GPIO16, Mod1.TXD
  N4: U1.GPIO17, Mod1.RXD
  N5: LED1.cathode, R1.Pin_1

custom parts:
  ESP32-38PinWide: Generic 38-Pin ESP32 with wide format (only access to one side of pins on a breadboard) based on Stephen Lilley's HiLetgo ESP-WROOM-32 ESP32 ESP-32S Development Board.
  SDS011 - dust sensor: The SDS 011 Sensor is a quite recent Air Quality Sensor developed by inovafit, a spin-off from the university of Jinan (in Shandong). With its size, it is probably one of the best sensor in terms of accuracy: While other sensors tend to focus on shrinking the sensor size, the SDS 011 has opted for a size tradeoff allowing it to use a larger fan. And the larger the fan, the better the quality.
