# Fritzing sketch WaterQuality (saved by Fritzing 1.0.7)
breadboards: 1

parts:
  U1 = ESP32-38PinWide [part_number=ESP32-38PinWide]
  S1 = Pushbutton [package="[THT]"]
  LED1 = LED - 5mm [color="Yellow (595nm)" current=0.030A package="5 mm [THT]"]
  R1 = Resistor [tolerance=±5% power=0.25W resistance=220 package=THT]
  DS1 = DS18B20 1-Wire Temperature Sensor Probe
  A1 = tds-sensor-meter-v1.0_1
  U2 = DFRobot SEN0189 [package=THT]
  R2 = Resistor [tolerance=±5% power=0.25W resistance=4.7k package=THT]

nets:
  N1: U1.3.3, DS1.VDD, A1.pin2, U2.P1_2, R2.Pin_1
  N2: U1.GPIO35, A1.pin1
  N3: U1.GPIO32, U2.P1_1
  N4: U1.GPIO26, LED1.anode
  N5: U1.GPIO27, S1.Pin_3, S1.Pin_4
  GND: U1.GND, R1.Pin_0, DS1.GND, A1.pin3, U2.P1_3
  N6: U1.GPIO4, DS1.DQ, R2.Pin_0
  N7: LED1.cathode, R1.Pin_1

custom parts:
  ESP32-38PinWide: Generic 38-Pin ESP32 with wide format (only access to one side of pins on a breadboard) based on Stephen Lilley's HiLetgo ESP-WROOM-32 ESP32 ESP-32S Development Board.
  : TDS Meter V1.0 Development Board Water Meter Filter Measuring Water Sensor Module.
  DFRobot SEN0189: Turbidity sensor of DFRobot SEN0189
