# Fritzing sketch ThermostatESPNow (saved by Fritzing 1.0.7)
breadboards: 1

parts:
  U1 = ESP32-38PinWide [part_number=ESP32-38PinWide]
  LCD1 = 2.8" SPI TFT Module [part_number=MSP2807]
  S1 = Pushbutton [package="[THT]"]
  S2 = Pushbutton [package="[THT]"]
  DS1 = DS18B20 1-Wire Temperature Sensor [part_number=DS18B20]
  R1 = Resistor [tolerance=±5% power=0.25W resistance=4.7k package=THT]
  U2 = Module 4 Relais 5V [package="Module 4 Relais 5V"]

nets:
  N1: U1.3.3, LCD1.pin1, DS1.VDD, R1.Pin_1
  N2: U1.GPIO32, U2.IN3
  N3: U1.GPIO33, U2.IN2
  N4: U1.GPIO26, DS1.DQ, R1.Pin_0
  N5: U1.GPIO27, S2.Pin_3, S2.Pin_4
  N6: U1.GPIO14, U2.IN4
  GND: U1.GND, LCD1.pin2, S1.Pin_1, S1.Pin_2, S2.Pin_1, S2.Pin_2, DS1.GND, U2.GND
  N7: U1.GPIO13, U2.IN1
  VIN: U1.VIN, U2.VCC
  N8: U1.GPIO15, LCD1.pin8
  N9: U1.GPIO2, LCD1.pin5
  N10: U1.GPIO4, LCD1.pin4
  N11: U1.GPIO16, S1.Pin_3, S1.Pin_4
  N12: U1.GPIO5, LCD1.pin3
  N13: U1.GPIO18, LCD1.pin7, LCD1.pin10
  N14: U1.GPIO19, LCD1.pin9, LCD1.pin13
  N15: U1.GPIO21, LCD1.pin11
  N16: U1.GPIO22, LCD1.pin14
  N17: U1.GPIO23, LCD1.pin6, LCD1.pin12

custom parts:
  ESP32-38PinWide: Generic 38-Pin ESP32 with wide format (only access to one side of pins on a breadboard) based on Stephen Lilley's HiLetgo ESP-WROOM-32 ESP32 ESP-32S Development Board.
  2.8" SPI TFT Module: A generic 2.8 inch LCD TFT 320x240 display with touchscreen and SD card slot. Uses the ILI9341 controller, like the Adafruit displays of this size uses.
  Module 4 Relais 5V: Module 4 Relais 5V 4x SPD-06VDC-SD-C
