# Fritzing sketch RFIDESPNow (saved by Fritzing 1.0.7)
breadboards: 1

parts:
  U1 = ESP32-38PinWide [part_number=ESP32-38PinWide]
  Componente1 = RFID-RC522-v2
  M1 = 1 chan 5v relay module
  LED1 = RGB LED (com. cathode, rgb) [color="Red (633nm)" current=0.030A package="5 mm [THT]"]
  S1 = Momentary Switch [package=ksa_sealed_tac_switch]
  R1 = Resistor [tolerance=±5% resistance=220 package="0805 [SMD]"]
  R2 = Resistor [tolerance=±5% resistance=220 package="0805 [SMD]"]
  R3 = Resistor [tolerance=±5% resistance=220 package="0805 [SMD]"]

nets:
  N1: U1.3.3, Componente1.3.3V
  N2: U1.GPIO33, S1.3
  GND: U1.GND, Componente1.GND, M1.pin_2, LED1.common_cathode
  N3: U1.VIN, M1.pin_1
  N4: U1.GPIO4, R3.Pin_1
  N5: U1.GPIO16, R2.Pin_1
  N6: U1.GPIO17, R1.Pin_0
  N7: U1.GPIO5, M1.pin_3
  N8: U1.GPIO18, Componente1.SCK
  N9: U1.GPIO19, Componente1.MISO
  N10: U1.GPIO21, Componente1.SDA
  N11: U1.GPIO22, Componente1.RST
  N12: U1.GPIO23, Componente1.MOSI
  N13: LED1.red_anode, R1.Pin_1
  N14: LED1.green_anode, R2.Pin_0
  N15: LED1.blue_anode, R3.Pin_0

custom parts:
  ESP32-38PinWide: Generic 38-Pin ESP32 with wide format (only access to one side of pins on a breadboard) based on Stephen Lilley's HiLetgo ESP-WROOM-32 ESP32 ESP-32S Development Board.
  RFID-RC522-v2: A simple China made RFID-RC522 Reader; do check the pin labels, as this is a MFRC522 based clone.
  1 chan 5v relay module: 1 Channel 5V Relay Module Board Shield with Optocoupler Support High and Low Level Trigger for Arduino.
