# Fritzing sketch WindowSensorESPNow (saved by Fritzing 1.0.7)
breadboards: 1

parts:
  U1 = ESP32-38PinWide [part_number=ESP32-38PinWide]
  S1 = Pushbutton [package="[SMD]"]
  LED1 = smd LED [color="Red (633nm)" package="0603 [SMD]"]
  R1 = Resistor [tolerance=±5% resistance=220 package="0603 [SMD]"]
  S2 = SWITCH-MOMENTARY-2 [package=reed_switch_plastic]

nets:
  N1: U1.GPIO32, LED1.anode
  N2: U1.GPIO33, S2.1
  N3: U1.GPIO27, S1.Pin_3, S1.Pin_4
  N4: U1.GND, S1.Pin_1, S1.Pin_2, R1.Pin_0, S2.2
  N5: LED1.cathode, R1.Pin_1

custom parts:
  ESP32-38PinWide: Generic 38-Pin ESP32 with wide format (only access to one side of pins on a breadboard) based on Stephen Lilley's HiLetgo ESP-WROOM-32 ESP32 ESP-32S Development Board.
