# Fritzing sketch PulseOximeter (saved by Fritzing 1.0.7)
breadboards: 1

parts:
  M1 = MakerFocus MAX30102
  OLED_I2C1 = OLED 128x64 I2C Monochrome Display
  U1 = ESP32-38PinWide [part_number=ESP32-38PinWide]

nets:
  GND: M1.GND, OLED_I2C1.GND, U1.GND
  N1: M1.SCL, OLED_I2C1.SCK, U1.GPIO22
  N2: M1.SDA, OLED_I2C1.SDA, U1.GPIO21
  VIN: M1.VIN, OLED_I2C1.VDD, U1.3.3

custom parts:
  MakerFocus MAX30102: Oximeter module using the MAX30102 chip. As usual, if you want the mounting holes in pcb, you need to drag a hole over the pad in silkscreen to actually drill the hole (by default they are not drilled)
  ESP32-38PinWide: Generic 38-Pin ESP32 with wide format (only access to one side of pins on a breadboard) based on Stephen Lilley's HiLetgo ESP-WROOM-32 ESP32 ESP-32S Development Board.
