# Fritzing sketch Videodoorphone (saved by Fritzing 1.0.7)
breadboards: 1

parts:
  U1 = Freenove ESP32-S3 CAM Board (FNK0085/86) [package=THT]
  Componente1 = Adafruit MAX98357A I2S 3W Class D Amplifier [part_number="Adafruit #3006"]
  Componente2 = INMP441
  S1 = Pushbutton [package="[THT]"]
  LED1 = LED - 5mm [color="Green (555nm)" current=0.030A package="5 mm [THT]"]
  R1 = Resistor [tolerance=±5% power=0.25W resistance=220 package=THT]
  M1 = 1 chan 5v relay module
  SP1 = SPEAKER [package=pcb_mount_speaker]

nets:
  3V3: U1.3V3, Componente2.VDD
  N1: U1.GPIO14, Componente2.SCK
  5V: U1.5V, Componente1.VIN, M1.pin_1
  N2: U1.GPIO1, Componente2.WS
  N3: U1.GPIO42, M1.pin_3
  N4: U1.GPIO41, S1.Pin_3, S1.Pin_4
  N5: U1.GPIO39, Componente1.BCLK
  N6: U1.GPIO38, Componente1.LRCLK
  N7: U1.GPIO48, R1.Pin_0
  N8: U1.GPIO47, Componente1.DIN
  N9: U1.GPIO21, Componente2.SD
  GND: U1.GND, Componente1.GND, Componente2.L/R, Componente2.GND, S1.Pin_1, S1.Pin_2, LED1.cathode, M1.pin_2
  N10: Componente1.VO-, SP1.+
  N11: Componente1.VO+, SP1.-
  N12: LED1.anode, R1.Pin_1

custom parts:
  Freenove ESP32-S3 CAM Board (FNK0085/86): Freenove ESP32-S3 CAM (kit "ESP32 ESP32-S3 Camera Board Kit")
  Adafruit MAX98357A I2S 3W Class D Amplifier: Listen to this good news - we now have an all in one digital audio amp breakout board that works incredibly well with the Raspberry Pi! If you're looking for an easy and low cost way to get you digital sound files bumpin' then the MAX08357 I2S Amp Breakout is for you. It takes standard I2S digital audio input and, not only decodes it into analog, but also amplifies it directly into a speaker.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
  INMP441: This is a simple breakout board for the INMP441 I2S MEMS microphone.
  1 chan 5v relay module: 1 Channel 5V Relay Module Board Shield with Optocoupler Support High and Low Level Trigger for Arduino.
