# Fritzing sketch TinyML_VoiceRelay (saved by Fritzing 1.0.7)
breadboards: 1

parts:
  U1 = ESP32-38PinWide [part_number=ESP32-38PinWide]
  OLED_I2C1 = OLED 128x64 I2C Monochrome Display
  Componente1 = INMP441
  S1 = Pushbutton [package="[THT]"]
  U2 = Module 4 Relais 5V [package="Module 4 Relais 5V"]

nets:
  VDD: U1.3.3, OLED_I2C1.VDD, Componente1.VDD
  N1: U1.GPIO33, Componente1.SD
  N2: U1.GPIO25, Componente1.WS
  N3: U1.GPIO26, Componente1.SCK
  N4: U1.GPIO27, S1.Pin_3, S1.Pin_4
  GND: U1.GND, OLED_I2C1.GND, Componente1.L/R, Componente1.GND, S1.Pin_1, S1.Pin_2, U2.GND
  VIN: U1.VIN, U2.VCC
  N5: U1.GPIO16, U2.IN1
  N6: U1.GPIO17, U2.IN2
  N7: U1.GPIO18, U2.IN3
  N8: U1.GPIO19, U2.IN4
  N9: U1.GPIO21, OLED_I2C1.SDA
  N10: U1.GPIO22, OLED_I2C1.SCK

custom parts:
  ESP32-38PinWide: Generic 38-Pin ESP32 with wide format (only access to one side of pins on a breadboard) based on Stephen Lilley's HiLetgo ESP-WROOM-32 ESP32 ESP-32S Development Board.
  INMP441: This is a simple breakout board for the INMP441 I2S MEMS microphone.
  Module 4 Relais 5V: Module 4 Relais 5V 4x SPD-06VDC-SD-C
